// Logisim project CircuitoN-E.circ as structural Verilog: 4 circuits, main circuit função
module \função  (
  input  A,
  input  B,
  input  C,
  output S
);

  wire e_1_s, e_2_s, e_3_s, e_4_s, e_5_s, e_6_s, e_7_s, e_8_s, e_9_s, e_10_s, e_11_s, e_12_s, e_13_s, e_14_s,
       \não_1_s , \não_2_s , \não_3_s , \não_4_s , \não_5_s , \não_6_s , \não_7_s , \não_8_s , \não_9_s ,
       \não_10_s , \não_11_s , \não_12_s , ou_1_s, ou_2_s, ou_3_s, ou_4_s, ou_5_s;

  \NÃO  \não_1  (.A(A), .S(\não_1_s ));
  \NÃO  \não_2  (.A(B), .S(\não_2_s ));
  \NÃO  \não_3  (.A(C), .S(\não_3_s ));
  \NÃO  \não_4  (.A(A), .S(\não_4_s ));
  \NÃO  \não_5  (.A(B), .S(\não_5_s ));
  \NÃO  \não_6  (.A(A), .S(\não_6_s ));
  \NÃO  \não_7  (.A(C), .S(\não_7_s ));
  \NÃO  \não_8  (.A(A), .S(\não_8_s ));
  \NÃO  \não_9  (.A(B), .S(\não_9_s ));
  \NÃO  \não_10  (.A(C), .S(\não_10_s ));
  \NÃO  \não_11  (.A(B), .S(\não_11_s ));
  \NÃO  \não_12  (.A(C), .S(\não_12_s ));
  E e_1 (.A(\não_2_s ), .B(\não_3_s ), .S(e_1_s));
  E e_2 (.A(\não_4_s ), .B(\não_5_s ), .S(e_2_s));
  E e_3 (.A(\não_6_s ), .B(\não_7_s ), .S(e_3_s));
  E e_4 (.A(\não_8_s ), .B(B), .S(e_4_s));
  E e_5 (.A(\não_9_s ), .B(\não_10_s ), .S(e_5_s));
  E e_6 (.A(A), .B(\não_11_s ), .S(e_6_s));
  E e_7 (.A(B), .B(\não_12_s ), .S(e_7_s));
  E e_8 (.A(\não_1_s ), .B(e_1_s), .S(e_8_s));
  E e_9 (.A(e_2_s), .B(C), .S(e_9_s));
  E e_10 (.A(B), .B(e_3_s), .S(e_10_s));
  E e_11 (.A(e_4_s), .B(C), .S(e_11_s));
  E e_12 (.A(A), .B(e_5_s), .S(e_12_s));
  E e_13 (.A(e_6_s), .B(C), .S(e_13_s));
  E e_14 (.A(A), .B(e_7_s), .S(e_14_s));
  OU ou_1 (.A(e_8_s), .B(e_9_s), .S(ou_1_s));
  OU ou_2 (.A(e_10_s), .B(e_11_s), .S(ou_2_s));
  OU ou_3 (.A(e_12_s), .B(e_13_s), .S(ou_3_s));
  OU ou_4 (.A(ou_1_s), .B(ou_2_s), .S(ou_4_s));
  OU ou_5 (.A(ou_3_s), .B(e_14_s), .S(ou_5_s));
  OU ou_6 (.A(ou_4_s), .B(ou_5_s), .S(S));
endmodule

module \NÃO  (
  input  A,
  output S
);

  nand nand_1 (S, A, A);
endmodule

module E (
  input  A,
  input  B,
  output S
);

  wire nand_1_out;

  nand nand_1 (nand_1_out, A, B);
  nand nand_2 (S, nand_1_out, nand_1_out);
endmodule

module OU (
  input  A,
  input  B,
  output S
);

  wire nand_1_out, nand_2_out;

  nand nand_1 (nand_1_out, A, A);
  nand nand_2 (nand_2_out, B, B);
  nand nand_3 (S, nand_1_out, nand_2_out);
endmodule
