// Logisim project somador4bits.circ as structural Verilog: 3 circuits, main circuit main
module main (
  input  a0,
  input  a1,
  input  a2,
  input  a3,
  input  b0,
  input  b1,
  input  b2,
  input  b3,
  output Overflow
);

  wire meio_somador_1_co0, meio_somador_1_s0, somador_completo_1_co, somador_completo_1_si,
       somador_completo_2_co, somador_completo_2_si, somador_completo_3_si;

  LED led_1 (.in(somador_completo_3_si));
  Meio_somador meio_somador_1 (.a0(a0), .b0(b0), .s0(meio_somador_1_s0), .co0(meio_somador_1_co0));
  LED led_2 (.in(somador_completo_1_si));
  LED led_3 (.in(meio_somador_1_s0));
  LED led_4 (.in(somador_completo_2_si));
  Somador_completo somador_completo_1 (
    .ai(a1), .ci(meio_somador_1_co0), .bi(b1), .si(somador_completo_1_si), .co(somador_completo_1_co));
  Somador_completo somador_completo_2 (
    .ai(a2), .ci(somador_completo_1_co), .bi(b2), .si(somador_completo_2_si), .co(somador_completo_2_co));
  Somador_completo somador_completo_3 (
    .ai(a3), .ci(somador_completo_2_co), .bi(b3), .si(somador_completo_3_si), .co(Overflow));
endmodule

module Meio_somador (
  input  a0,
  input  b0,
  output s0,
  output co0
);

  xor xor_1 (s0, a0, b0);
  and and_1 (co0, a0, b0);
endmodule

module Somador_completo (
  input  ai,
  input  ci,
  input  bi,
  output si,
  output co
);

  wire and_1_out, and_2_out, and_3_out, or_1_out, xor_1_out;

  xor xor_1 (xor_1_out, ai, bi);
  and and_1 (and_1_out, ai, ci);
  and and_2 (and_2_out, ai, bi);
  and and_3 (and_3_out, ci, bi);
  xor xor_2 (si, ci, xor_1_out);
  or or_1 (or_1_out, and_1_out, and_2_out);
  or or_2 (co, or_1_out, and_3_out);
endmodule
